# Fritzing sketch AlarmMonitor (saved by Fritzing 0.9.3b)
breadboards: 2

parts:
  ESP1 = ESP32-DevkitC
  Part1 = RFID-RC522-v3
  J1 = Piezo Speaker
  J2 = Piezo Speaker
  BUTTON1 = Waterproof Pushbutton (red)
  BUTTON2 = Waterproof Pushbutton (blue)
  J3 = Camdenboss CTB0158-10 [part_number=CTB0158-10 package=THT]  # not connected
  J4 = Camdenboss CTB0158-5 [part_number=CTB0158-5 package=THT]  # not connected
  R2 = Resistor [tolerance=±5% resistance=100 package=THT]
  R1 = Resistor [tolerance=±5% resistance=470 package=THT]
  R3 = Resistor [tolerance=±5% resistance=100k package=THT]
  R4 = Resistor [tolerance=±5% resistance=100k package=THT]
  R5 = Resistor [tolerance=±5% resistance=100k package=THT]
  R6 = Resistor [tolerance=±5% resistance=100k package=THT]
  TFT1 = 2.8 320x240 TFT SPI Display, ILI9341 Controller Chip  # not connected

nets:
  3V3: ESP1.3V3, Part1.3.3V, R2.Pin_0, R1.Pin_1
  N1: ESP1.SENSOR_VP, R5.Pin_0
  N2: ESP1.SENSOR_VN, R4.Pin_0
  N3: ESP1.IO34, R6.Pin_0
  N4: ESP1.IO35, R3.Pin_0
  N5: ESP1.IO14, BUTTON2.no_name_yet#2
  N6: ESP1.IO12, BUTTON1.no_name_yet#2
  GND: ESP1.GND, Part1.GND, J1.pin1, J2.pin1, R3.Pin_1, R4.Pin_1, R5.Pin_1, R6.Pin_1
  N7: ESP1.IO19, Part1.MISO
  N8: ESP1.IO18, ESP1.IO2, Part1.SCK
  N9: ESP1.IO17, Part1.SDA
  N10: ESP1.IO16, Part1.RST
  N11: ESP1.IO4, J2.pin2
  N12: ESP1.IO15, J1.pin2
  N13: ESP1.IO13, BUTTON1.no_name_yet#5, BUTTON2.no_name_yet#5
  N14: ESP1.IO23, Part1.MOSI
  N15: BUTTON1.no_name_yet#1, BUTTON1.no_name_yet#4, R1.Pin_0
  N16: BUTTON2.no_name_yet#1, BUTTON2.no_name_yet#4, R2.Pin_1

custom parts:
  RFID-RC522-v3: A simple China made RFID-RC522 Reader (6x4 cm); do check the pin labels, as this is a MFRC522 based clone.
  Waterproof Pushbutton (red): Waterproof Illuminated Pushbutton (red)
  Waterproof Pushbutton (blue): Waterproof Illuminated Pushbutton (blue)
  2.8 320x240 TFT SPI Display, ILI9341 Controller Chip: 2.8" TFT SPI Display with ILI9341 Controller and SD Card reader
